# Fritzing sketch erfinder-weihnachtsbaum-raspi (saved by Fritzing 0.9.3b)
circuit board: 9.00999cm x 11.6501cm
breadboards: 1

parts:
  LED1 = LED - 5mm [color="Yellow (585nm)" package="5 mm [THT]"]
  LED2 = LED - 5mm [color="Red (633nm)" package="5 mm [THT]"]
  LED3 = LED - 5mm [color="Red (633nm)" package="5 mm [THT]"]
  R2 = Resistor [tolerance=±5% resistance=220 package=THT]
  R3 = Resistor [tolerance=±5% resistance=220 package=THT]
  R4 = Resistor [tolerance=±5% resistance=220 package=THT]
  R5 = Resistor [tolerance=±5% resistance=220 package=THT]
  LED5 = LED - 5mm [color="Red (633nm)" package="5 mm [THT]"]
  R6 = Resistor [tolerance=±5% resistance=220 package=THT]
  LED6 = LED - 5mm [color="Red (633nm)" package="5 mm [THT]"]
  LED7 = LED - 5mm [color="Red (633nm)" package="5 mm [THT]"]
  R7 = Resistor [tolerance=±5% resistance=220 package=THT]
  LED8 = LED - 5mm [color="Red (633nm)" package="5 mm [THT]"]
  R8 = Resistor [tolerance=±5% resistance=220 package=THT]
  LED9 = LED - 5mm [color="Red (633nm)" package="5 mm [THT]"]
  LED10 = LED - 5mm [color="Red (633nm)" package="5 mm [THT]"]
  LED11 = LED - 5mm [color="Red (633nm)" package="5 mm [THT]"]
  R9 = Resistor [tolerance=±5% resistance=220 package=THT]
  R10 = Resistor [tolerance=±5% resistance=220 package=THT]
  R11 = Resistor [tolerance=±5% resistance=220 package=THT]
  J1 = double row female pin header, 26 pins [form="♀ (female)"]

nets:
  N1: LED1.cathode, LED2.cathode, LED3.cathode, LED5.cathode, LED6.cathode, LED7.cathode, LED8.cathode, LED9.cathode, LED10.cathode, LED11.cathode, J1.pin5
  N2: LED1.anode, R4.Pin_0
  N3: LED2.anode, R2.Pin_0
  N4: LED3.anode, R3.Pin_0
  N5: R2.Pin_1, J1.pin22
  N6: R3.Pin_1, J1.pin15
  N7: R4.Pin_1, J1.pin4
  N8: R5.Pin_0, LED5.anode
  N9: R5.Pin_1, J1.pin14
  N10: R6.Pin_0, LED6.anode
  N11: R6.Pin_1, J1.pin12
  N12: LED7.anode, R7.Pin_0
  N13: R7.Pin_1, J1.pin23
  N14: LED8.anode, R8.Pin_0
  N15: R8.Pin_1, J1.pin21
  N16: LED9.anode, R9.Pin_0
  N17: LED10.anode, R10.Pin_0
  N18: LED11.anode, R11.Pin_0
  N19: R9.Pin_1, J1.pin16
  N20: R10.Pin_1, J1.pin18
  N21: R11.Pin_1, J1.pin19
